# Fritzing sketch CPU_Board_021 (saved by Fritzing 0.9.6b)
circuit board: 10.67cm x 7.87cm
breadboards: 1

parts:
  J4 = female pin header, 10 pins [form="♀ (female)"]
  J3 = female pin header, 10 pins [form="♀ (female)"]
  J2 = female pin header, 10 pins [form="♀ (female)"]
  J1 = female pin header, 10 pins [form="♀ (female)"]
  J4a = female pin header, 10 pins [form="♀ (female)"]
  J3a = female pin header, 10 pins [form="♀ (female)"]
  J2a = female pin header, 10 pins [form="♀ (female)"]
  J1a = female pin header, 10 pins [form="♀ (female)"]
  J9 = female pin header, 31 pins [form="♀ (female)"]  # not connected
  J6 = male pin header, 5 pins [form="♂ (male)"]
  J7 = female pin header, 42 pins [form="♀ (female)"]  # not connected
  J19 = female pin header, 20 pins [form="♀ (female)"]  # not connected
  J8 = female pin header, 21 pins [form="♀ (female)"]  # not connected
  M1 = DOIT Esp32 DevKit v1 (30 pins long, 11 pins width) [part_number=ESP32S-PIN30]
  P1 = MP1584 [package=THT]

nets:
  +24V: J4.pin1, J3.pin1, J2.pin1, J1.pin1, J4a.pin1, J3a.pin1, J2a.pin1, J1a.pin1
  N1: J4.pin2, J4a.pin2
  N2: J4.pin3, J4a.pin3
  N3: J4.pin4, J4a.pin4
  N4: J4.pin5, J4a.pin5
  N5: J4.pin6, J4a.pin6
  N6: J4.pin7, J4a.pin7
  N7: J4.pin8, J4a.pin8
  N8: J4.pin9, J4a.pin9
  GND: J4.pin10, J3.pin10, J2.pin10, J1.pin10, J4a.pin10, J3a.pin10, J2a.pin10, J1a.pin10
  N9: J3.pin2, J3a.pin2
  N10: J3.pin3, J3a.pin3
  N11: J3.pin4, J3a.pin4
  N12: J3.pin5, J3a.pin5
  N13: J3.pin6, J3a.pin6
  N14: J3.pin7, J3a.pin7
  N15: J3.pin8, J3a.pin8
  N16: J3.pin9, J3a.pin9
  N17: J2.pin2, J2a.pin2
  N18: J2.pin3, J2a.pin3
  N19: J2.pin4, J2a.pin4
  N20: J2.pin5, J2a.pin5
  N21: J2.pin6, J2a.pin6
  N22: J2.pin7, J2a.pin7
  N23: J2.pin8, J2a.pin8
  N24: J2.pin9, J2a.pin9
  N25: J1.pin2, J1a.pin2
  N26: J1.pin3, J1a.pin3
  N27: J1.pin4, J1a.pin4
  N28: J1.pin5, J1a.pin5
  N29: J1.pin6, J1a.pin6
  N30: J1.pin7, J1a.pin7
  N31: J1.pin8, J1a.pin8
  N32: J1.pin9, J1a.pin9
  N33: J6.pin1, M1.GND, P1.pin5
  N34: J6.pin2, M1.D21
  N35: J6.pin3, M1.3V3
  N36: J6.pin4, M1.D22
  N37: M1.VIN, P1.pin7

notes:
  Sda
  Scl
  +3V3
  Gnd
  +24v
  I2C Bus
  Cpu-PCB  - IHC-Replacement
  V.021 20241209 19:35

custom parts:
  DOIT Esp32 DevKit v1 (30 pins long, 11 pins width): The DOIT Esp32 DevKit v1 is one of the development board created by DOIT to evaluate the ESP-WROOM-32 module. It is based on the ESP32 microcontroller that boasts Wifi, Bluetooth, Ethernet and Low Power support all in a single chip. (vanepp) made breadboard work, adjusted pin numbering and labels and reduced size of schematic and cleaned up pcb. This chip is 30pins long (2 x15) and 11 pins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
  MP1584: 3A, 1.5MHz, 28V Step-Down Converter
