# Fritzing sketch Input_Board_021 (saved by Fritzing 0.9.6b)
circuit board: 10.67cm x 7.87cm
breadboards: 1

parts:
  IC2 = MCP20017 [part_number=MCP23017 package="DIP (Dual Inline) [THT]"]
  IC1 = MCP20017 [part_number=MCP23017 package="DIP (Dual Inline) [THT]"]
  C1 = Ceramic Capacitor [capacitance=100nF voltage=35V package="100 mil [THT, multilayer]"]
  C2 = Ceramic Capacitor [capacitance=100nF voltage=35V package="100 mil [THT, multilayer]"]
  IC3 = ULN2803A [package=THT]
  IC4 = ULN2803A [package=THT]
  IC5 = ULN2803A [package=THT]
  D2 = 1N4148 [package=1n4148-SMD_1206]
  D15 = 1N4148 [package=1n4148-SMD_1206]
  D13 = 1N4148 [package=1n4148-SMD_1206]
  D11 = 1N4148 [package=1n4148-SMD_1206]
  D9 = 1N4148 [package=1n4148-SMD_1206]
  D7 = 1N4148 [package=1n4148-SMD_1206]
  D5 = 1N4148 [package=1n4148-SMD_1206]
  D3 = 1N4148 [package=1n4148-SMD_1206]
  D1 = 1N4148 [package=1n4148-SMD_1206]
  D4 = 1N4148 [package=1n4148-SMD_1206]
  D6 = 1N4148 [package=1n4148-SMD_1206]
  D8 = 1N4148 [package=1n4148-SMD_1206]
  D10 = 1N4148 [package=1n4148-SMD_1206]
  D12 = 1N4148 [package=1n4148-SMD_1206]
  D14 = 1N4148 [package=1n4148-SMD_1206]
  D16 = 1N4148 [package=1n4148-SMD_1206]
  D32 = 1N4148 [package=1n4148-SMD_1206]
  D30 = 1N4148 [package=1n4148-SMD_1206]
  D28 = 1N4148 [package=1n4148-SMD_1206]
  D26 = 1N4148 [package=1n4148-SMD_1206]
  D24 = 1N4148 [package=1n4148-SMD_1206]
  D22 = 1N4148 [package=1n4148-SMD_1206]
  D20 = 1N4148 [package=1n4148-SMD_1206]
  D18 = 1N4148 [package=1n4148-SMD_1206]
  D17 = 1N4148 [package=1n4148-SMD_1206]
  D19 = 1N4148 [package=1n4148-SMD_1206]
  D21 = 1N4148 [package=1n4148-SMD_1206]
  D23 = 1N4148 [package=1n4148-SMD_1206]
  D25 = 1N4148 [package=1n4148-SMD_1206]
  D27 = 1N4148 [package=1n4148-SMD_1206]
  D29 = 1N4148 [package=1n4148-SMD_1206]
  D31 = 1N4148 [package=1n4148-SMD_1206]
  D48 = 1N4148 [package=1n4148-SMD_1206]
  D46 = 1N4148 [package=1n4148-SMD_1206]
  D44 = 1N4148 [package=1n4148-SMD_1206]
  D42 = 1N4148 [package=1n4148-SMD_1206]
  D40 = 1N4148 [package=1n4148-SMD_1206]
  D38 = 1N4148 [package=1n4148-SMD_1206]
  D36 = 1N4148 [package=1n4148-SMD_1206]
  D34 = 1N4148 [package=1n4148-SMD_1206]
  D33 = 1N4148 [package=1n4148-SMD_1206]
  D35 = 1N4148 [package=1n4148-SMD_1206]
  D37 = 1N4148 [package=1n4148-SMD_1206]
  D39 = 1N4148 [package=1n4148-SMD_1206]
  D41 = 1N4148 [package=1n4148-SMD_1206]
  D43 = 1N4148 [package=1n4148-SMD_1206]
  D45 = 1N4148 [package=1n4148-SMD_1206]
  D47 = 1N4148 [package=1n4148-SMD_1206]
  D50 = 1N4148 [package=1n4148-SMD_1206]
  D52 = 1N4148 [package=1n4148-SMD_1206]
  D54 = 1N4148 [package=1n4148-SMD_1206]
  D56 = 1N4148 [package=1n4148-SMD_1206]
  D58 = 1N4148 [package=1n4148-SMD_1206]
  D60 = 1N4148 [package=1n4148-SMD_1206]
  D62 = 1N4148 [package=1n4148-SMD_1206]
  D64 = 1N4148 [package=1n4148-SMD_1206]
  D49 = 1N4148 [package=1n4148-SMD_1206]
  D51 = 1N4148 [package=1n4148-SMD_1206]
  D53 = 1N4148 [package=1n4148-SMD_1206]
  D55 = 1N4148 [package=1n4148-SMD_1206]
  D57 = 1N4148 [package=1n4148-SMD_1206]
  D63 = 1N4148 [package=1n4148-SMD_1206]
  D61 = 1N4148 [package=1n4148-SMD_1206]
  D59 = 1N4148 [package=1n4148-SMD_1206]
  IC6 = ULN2803A [package=THT]
  J4 = female pin header, 10 pins [form="♀ (female)"]
  J3 = female pin header, 10 pins [form="♀ (female)"]
  J2 = female pin header, 10 pins [form="♀ (female)"]
  J1 = female pin header, 10 pins [form="♀ (female)"]
  J4a = female pin header, 10 pins [form="♀ (female)"]
  J3a = female pin header, 10 pins [form="♀ (female)"]
  J2a = female pin header, 10 pins [form="♀ (female)"]
  J1a = female pin header, 10 pins [form="♀ (female)"]
  J9 = female pin header, 31 pins [form="♀ (female)"]  # not connected
  J11 = female pin header, 1 pin [form="♀ (female)"]
  J12 = female pin header, 1 pin [form="♀ (female)"]
  J13 = female pin header, 2 pins [form="♀ (female)"]
  J14 = female pin header, 2 pins [form="♀ (female)"]
  J5 = male pin header, 5 pins [form="♂ (male)"]
  J6 = male pin header, 5 pins [form="♂ (male)"]
  R36 = Resistor [tolerance=±5% resistance=10k power=0.25 package="1206 [SMD]"]
  R35 = Resistor [tolerance=±5% resistance=10k power=0.25 package="1206 [SMD]"]
  J15 = female pin header, 8 pins [form="♀ (female)"]
  J16 = female pin header, 8 pins [form="♀ (female)"]
  J17 = female pin header, 8 pins [form="♀ (female)"]
  J18 = female pin header, 8 pins [form="♀ (female)"]
  J7 = female pin header, 42 pins [form="♀ (female)"]  # not connected
  J19 = female pin header, 20 pins [form="♀ (female)"]  # not connected
  J8 = female pin header, 21 pins [form="♀ (female)"]  # not connected

nets:
  N1: IC2.GPB0, D50.C, D49.A, IC6.In_8
  N2: IC2.GPB1, D52.C, D51.A, IC6.In_7
  N3: IC2.GPB2, D54.C, D53.A, IC6.In_6
  N4: IC2.GPB3, D56.C, D55.A, IC6.In_5
  N5: IC2.GPB04, D58.C, D57.A, IC6.In_4
  N6: IC2.GPB5, D60.C, D59.A, IC6.In_3
  N7: IC2.GPB6, D62.C, D61.A, IC6.In_2
  N8: IC2.GPB8, D64.C, D63.A, IC6.In_1
  +3V3: IC2.VDD, IC2.A0, IC2.RESET, IC1.VDD, IC1.RESET, C1.0, C2.0, D15.C, D13.C, D11.C, D9.C, D7.C, D5.C, D3.C, D1.C, D17.C, D19.C, D21.C, D23.C, D25.C, D27.C, D29.C, D31.C, D33.C, D35.C, D37.C, D39.C, D41.C, D43.C, D45.C, D47.C, D49.C, D51.C, D53.C, D55.C, D57.C, D63.C, D61.C, D59.C, J14.pin1, J14.pin2, J5.pin3, J6.pin3, R36.Pin_0, R35.Pin_1
  GND: IC2.GND, IC1.GND, IC1.A0, C1.1, C2.1, IC3.0V, IC4.0V, IC5.0V, D2.A, D4.A, D6.A, D8.A, D10.A, D12.A, D14.A, D16.A, D32.A, D30.A, D28.A, D26.A, D24.A, D22.A, D20.A, D18.A, D48.A, D46.A, D44.A, D42.A, D40.A, D38.A, D36.A, D34.A, D50.A, D52.A, D54.A, D56.A, D58.A, D60.A, D62.A, D64.A, IC6.0V, J4.pin10, J3.pin10, J2.pin10, J1.pin10, J4a.pin10, J3a.pin10, J2a.pin10, J1a.pin10, J13.pin1, J13.pin2, J5.pin1, J6.pin1
  SCL: IC2.SCL, IC1.SCL, J5.pin4, J6.pin4, R36.Pin_1
  SDA: IC2.SDA, IC1.SDA, J5.pin2, J6.pin2, R35.Pin_0
  A1: IC2.A1, IC1.A1, J12.pin1
  A2: IC2.A2, IC1.A2, J11.pin1
  N9: IC2.GPA0, IC5.In_8, D34.C, D33.A
  N10: IC2.GPA1, IC5.In_7, D36.C, D35.A
  N11: IC2.GPA2, IC5.In_6, D38.C, D37.A
  N12: IC2.GPA3, IC5.In_5, D40.C, D39.A
  N13: IC2.GPA4, IC5.In_4, D42.C, D41.A
  N14: IC2.GPA5, IC5.In_3, D44.C, D43.A
  N15: IC2.GPA6, IC5.In_2, D46.C, D45.A
  N16: IC2.GPA7, IC5.In_1, D48.C, D47.A
  N17: IC1.GPB0, IC4.In_8, D18.C, D17.A
  N18: IC1.GPB1, IC4.In_7, D20.C, D19.A
  N19: IC1.GPB2, IC4.In_6, D22.C, D21.A
  N20: IC1.GPB3, IC4.In_5, D24.C, D23.A
  N21: IC1.GPB04, IC4.In_4, D26.C, D25.A
  N22: IC1.GPB5, IC4.In_3, D28.C, D27.A
  N23: IC1.GPB6, IC4.In_2, D30.C, D29.A
  N24: IC1.GPB8, IC4.In_1, D32.C, D31.A
  N25: IC1.GPA0, IC3.In_8, D2.C, D1.A
  N26: IC1.GPA1, IC3.In_7, D3.A, D4.C
  N27: IC1.GPA2, IC3.In_6, D5.A, D6.C
  N28: IC1.GPA3, IC3.In_5, D7.A, D8.C
  N29: IC1.GPA4, IC3.In_4, D9.A, D10.C
  N30: IC1.GPA5, IC3.In_3, D11.A, D12.C
  N31: IC1.GPA6, IC3.In_2, D13.A, D14.C
  N32: IC1.GPA7, IC3.In_1, D15.A, D16.C
  +24V: IC3.COM_-_Common, IC4.COM_-_Common, IC5.COM_-_Common, IC6.COM_-_Common, J4.pin1, J3.pin1, J2.pin1, J1.pin1, J4a.pin1, J3a.pin1, J2a.pin1, J1a.pin1, J5.pin5, J6.pin5
  N33: IC3.Out_8, J1.pin2, J1a.pin2, J18.pin8
  N34: IC3.Out_7, J1.pin3, J1a.pin3, J18.pin7
  N35: IC3.Out_6, J1.pin4, J1a.pin4, J18.pin6
  N36: IC3.Out_5, J1.pin5, J1a.pin5, J18.pin5
  N37: IC3.Out_4, J1.pin6, J1a.pin6, J18.pin4
  N38: IC3.Out_3, J1.pin7, J1a.pin7, J18.pin3
  N39: IC3.Out_2, J1.pin8, J1a.pin8, J18.pin2
  N40: IC3.Out_1, J1.pin9, J1a.pin9, J18.pin1
  N41: IC4.Out_8, J2.pin2, J2a.pin2, J17.pin8
  N42: IC4.Out_7, J2.pin3, J2a.pin3, J17.pin7
  N43: IC4.Out_6, J2.pin4, J2a.pin4, J17.pin6
  N44: IC4.Out_5, J2.pin5, J2a.pin5, J17.pin5
  N45: IC4.Out_4, J2.pin6, J2a.pin6, J17.pin4
  N46: IC4.Out_3, J2.pin7, J2a.pin7, J17.pin3
  N47: IC4.Out_2, J2.pin8, J2a.pin8, J17.pin2
  N48: IC4.Out_1, J2.pin9, J2a.pin9, J17.pin1
  N49: IC5.Out_8, J3.pin2, J3a.pin2, J16.pin8
  N50: IC5.Out_7, J3.pin3, J3a.pin3, J16.pin7
  N51: IC5.Out_6, J3.pin4, J3a.pin4, J16.pin6
  N52: IC5.Out_5, J3.pin5, J3a.pin5, J16.pin5
  N53: IC5.Out_4, J3.pin6, J3a.pin6, J16.pin4
  N54: IC5.Out_3, J3.pin7, J3a.pin7, J16.pin3
  N55: IC5.Out_2, J3.pin8, J3a.pin8, J16.pin2
  N56: IC5.Out_1, J3.pin9, J3a.pin9, J16.pin1
  N57: IC6.Out_8, J4.pin2, J4a.pin2, J15.pin8
  N58: IC6.Out_7, J4.pin3, J4a.pin3, J15.pin7
  N59: IC6.Out_6, J4.pin4, J4a.pin4, J15.pin6
  N60: IC6.Out_5, J4.pin5, J4a.pin5, J15.pin5
  N61: IC6.Out_4, J4.pin6, J4a.pin6, J15.pin4
  N62: IC6.Out_3, J4.pin7, J4a.pin7, J15.pin3
  N63: IC6.Out_2, J4.pin8, J4a.pin8, J15.pin2
  N64: IC6.Out_1, J4.pin9, J4a.pin9, J15.pin1

notes:
  Gnd
  Sda
  +3V3
  Scl
  +24v
  Address Select
  Afkobling
  I2C Bus
  Ano
  Cat
  I/O-PCB  - IHC-Replacement
  V.021 20241208 20:00
  ADDR
  A1
  A2

custom parts:
  MCP20017: MCP23017, 28 pins on a 300mil dual inline package (DIP) footprint. 16-Bit I/O Expander with I2C Serial Interface
  1N4148: SMD 1206
