# Fritzing sketch Input_Board_010 (saved by Fritzing 0.9.6b)
circuit board: 20.95cm x 8cm
breadboards: 1

parts:
  IC1 = MCP20017 [part_number=MCP23017 package="DIP (Dual Inline) [THT]"]
  C2 = Ceramic Capacitor [capacitance=100nF voltage=35V package="100 mil [THT, multilayer]"]
  C1 = Ceramic Capacitor [capacitance=100nF voltage=35V package="100 mil [THT, multilayer]"]
  J4 = female pin header, 9 pins [form="♀ (female)"]
  J3 = female pin header, 9 pins [form="♀ (female)"]
  J2 = female pin header, 9 pins [form="♀ (female)"]
  J1 = female pin header, 9 pins [form="♀ (female)"]
  J4a = female pin header, 9 pins [form="♀ (female)"]
  J1a = female pin header, 9 pins [form="♀ (female)"]
  J2a = female pin header, 9 pins [form="♀ (female)"]
  J3a = female pin header, 9 pins [form="♀ (female)"]
  J8 = female pin header, 9 pins [form="♀ (female)"]
  J7 = female pin header, 9 pins [form="♀ (female)"]
  J5 = female pin header, 9 pins [form="♀ (female)"]
  J8a = female pin header, 9 pins [form="♀ (female)"]
  J5a = female pin header, 9 pins [form="♀ (female)"]
  J6 = female pin header, 9 pins [form="♀ (female)"]
  J7a = female pin header, 9 pins [form="♀ (female)"]
  IC2 = MCP20017 [part_number=MCP23017 package="DIP (Dual Inline) [THT]"]
  IC3 = MCP20017 [part_number=MCP23017 package="DIP (Dual Inline) [THT]"]
  IC4 = MCP20017 [part_number=MCP23017 package="DIP (Dual Inline) [THT]"]
  C3 = Ceramic Capacitor [capacitance=100nF voltage=35V package="100 mil [THT, multilayer]"]
  C4 = Ceramic Capacitor [capacitance=100nF voltage=35V package="100 mil [THT, multilayer]"]
  J10 = Screw terminal - 2 pins [package=THT]
  DC1 = HW-613 [part_number=HW-613-5V package=THT]
  Q1 = Basic FET P-Channel [part_number=FQP27P06 package="TO220 [THT]"]
  R1 = Resistor [tolerance=±5% power=0.25 resistance=1k package=THT]
  R2 = Resistor [tolerance=±5% power=0.25 resistance=1k package=THT]
  R3 = Resistor [tolerance=±5% power=0.25 resistance=1k package=THT]
  R4 = Resistor [tolerance=±5% power=0.25 resistance=1k package=THT]
  R5 = Resistor [tolerance=±5% power=0.25 resistance=1k package=THT]
  R6 = Resistor [tolerance=±5% power=0.25 resistance=1k package=THT]
  R7 = Resistor [tolerance=±5% power=0.25 resistance=1k package=THT]
  R8 = Resistor [tolerance=±5% power=0.25 resistance=1k package=THT]
  R9 = Resistor [tolerance=±5% power=0.25 resistance=1k package=THT]
  R10 = Resistor [tolerance=±5% power=0.25 resistance=1k package=THT]
  R11 = Resistor [tolerance=±5% power=0.25 resistance=1k package=THT]
  R12 = Resistor [tolerance=±5% power=0.25 resistance=1k package=THT]
  R13 = Resistor [tolerance=±5% power=0.25 resistance=1k package=THT]
  R14 = Resistor [tolerance=±5% power=0.25 resistance=1k package=THT]
  R15 = Resistor [tolerance=±5% power=0.25 resistance=1k package=THT]
  R16 = Resistor [tolerance=±5% power=0.25 resistance=1k package=THT]
  D1 = 1N4148 [package=1n4148-SMD_1206]
  D2 = 1N4148 [package=1n4148-SMD_1206]
  D3 = 1N4148 [package=1n4148-SMD_1206]
  D4 = 1N4148 [package=1n4148-SMD_1206]
  D6 = 1N4148 [package=1n4148-SMD_1206]
  D7 = 1N4148 [package=1n4148-SMD_1206]
  D8 = 1N4148 [package=1n4148-SMD_1206]
  R17 = Resistor [tolerance=±5% power=0.25 resistance=1k package=THT]
  R18 = Resistor [tolerance=±5% power=0.25 resistance=1k package=THT]
  R19 = Resistor [tolerance=±5% power=0.25 resistance=1k package=THT]
  R20 = Resistor [tolerance=±5% power=0.25 resistance=1k package=THT]
  R21 = Resistor [tolerance=±5% power=0.25 resistance=1k package=THT]
  R22 = Resistor [tolerance=±5% power=0.25 resistance=1k package=THT]
  R23 = Resistor [tolerance=±5% power=0.25 resistance=1k package=THT]
  R24 = Resistor [tolerance=±5% power=0.25 resistance=1k package=THT]
  R25 = Resistor [tolerance=±5% power=0.25 resistance=1k package=THT]
  R26 = Resistor [tolerance=±5% power=0.25 resistance=1k package=THT]
  R27 = Resistor [tolerance=±5% power=0.25 resistance=1k package=THT]
  R28 = Resistor [tolerance=±5% power=0.25 resistance=1k package=THT]
  R29 = Resistor [tolerance=±5% power=0.25 resistance=1k package=THT]
  R30 = Resistor [tolerance=±5% power=0.25 resistance=1k package=THT]
  R31 = Resistor [tolerance=±5% power=0.25 resistance=1k package=THT]
  R32 = Resistor [tolerance=±5% power=0.25 resistance=1k package=THT]
  D9 = 1N4148 [package=1n4148-SMD_1206]
  D10 = 1N4148 [package=1n4148-SMD_1206]
  D11 = 1N4148 [package=1n4148-SMD_1206]
  D12 = 1N4148 [package=1n4148-SMD_1206]
  D13 = 1N4148 [package=1n4148-SMD_1206]
  D14 = 1N4148 [package=1n4148-SMD_1206]
  D15 = 1N4148 [package=1n4148-SMD_1206]
  D16 = 1N4148 [package=1n4148-SMD_1206]
  D17 = 1N4148 [package=1n4148-SMD_1206]
  D18 = 1N4148 [package=1n4148-SMD_1206]
  D19 = 1N4148 [package=1n4148-SMD_1206]
  D20 = 1N4148 [package=1n4148-SMD_1206]
  D21 = 1N4148 [package=1n4148-SMD_1206]
  D22 = 1N4148 [package=1n4148-SMD_1206]
  D23 = 1N4148 [package=1n4148-SMD_1206]
  D24 = 1N4148 [package=1n4148-SMD_1206]
  D5 = 1N4148 [package=1n4148-SMD_1206]
  D25 = 1N4148 [package=1n4148-SMD_1206]
  D26 = 1N4148 [package=1n4148-SMD_1206]
  D27 = 1N4148 [package=1n4148-SMD_1206]
  D28 = 1N4148 [package=1n4148-SMD_1206]
  D29 = 1N4148 [package=1n4148-SMD_1206]
  D30 = 1N4148 [package=1n4148-SMD_1206]
  D31 = 1N4148 [package=1n4148-SMD_1206]
  D32 = 1N4148 [package=1n4148-SMD_1206]
  J6a = female pin header, 9 pins [form="♀ (female)"]
  D33 = 1N4148 [package=1n4148-SMD_1206]
  D34 = 1N4148 [package=1n4148-SMD_1206]
  D35 = 1N4148 [package=1n4148-SMD_1206]
  D36 = 1N4148 [package=1n4148-SMD_1206]
  D37 = 1N4148 [package=1n4148-SMD_1206]
  D38 = 1N4148 [package=1n4148-SMD_1206]
  D39 = 1N4148 [package=1n4148-SMD_1206]
  D40 = 1N4148 [package=1n4148-SMD_1206]
  D41 = 1N4148 [package=1n4148-SMD_1206]
  D42 = 1N4148 [package=1n4148-SMD_1206]
  D43 = 1N4148 [package=1n4148-SMD_1206]
  D44 = 1N4148 [package=1n4148-SMD_1206]
  D45 = 1N4148 [package=1n4148-SMD_1206]
  D46 = 1N4148 [package=1n4148-SMD_1206]
  D47 = 1N4148 [package=1n4148-SMD_1206]
  D48 = 1N4148 [package=1n4148-SMD_1206]
  D49 = 1N4148 [package=1n4148-SMD_1206]
  D50 = 1N4148 [package=1n4148-SMD_1206]
  D51 = 1N4148 [package=1n4148-SMD_1206]
  D52 = 1N4148 [package=1n4148-SMD_1206]
  D53 = 1N4148 [package=1n4148-SMD_1206]
  D54 = 1N4148 [package=1n4148-SMD_1206]
  D55 = 1N4148 [package=1n4148-SMD_1206]
  D56 = 1N4148 [package=1n4148-SMD_1206]
  D57 = 1N4148 [package=1n4148-SMD_1206]
  D58 = 1N4148 [package=1n4148-SMD_1206]
  D59 = 1N4148 [package=1n4148-SMD_1206]
  D60 = 1N4148 [package=1n4148-SMD_1206]
  D61 = 1N4148 [package=1n4148-SMD_1206]
  D62 = 1N4148 [package=1n4148-SMD_1206]
  D63 = 1N4148 [package=1n4148-SMD_1206]
  D64 = 1N4148 [package=1n4148-SMD_1206]
  R33 = Resistor [tolerance=±5% power=0.25 resistance=1k package=THT]
  R34 = Resistor [tolerance=±5% power=0.25 resistance=1k package=THT]
  R35 = Resistor [tolerance=±5% power=0.25 resistance=1k package=THT]
  R36 = Resistor [tolerance=±5% power=0.25 resistance=1k package=THT]
  R37 = Resistor [tolerance=±5% power=0.25 resistance=1k package=THT]
  R38 = Resistor [tolerance=±5% power=0.25 resistance=1k package=THT]
  R39 = Resistor [tolerance=±5% power=0.25 resistance=1k package=THT]
  R40 = Resistor [tolerance=±5% power=0.25 resistance=1k package=THT]
  R41 = Resistor [tolerance=±5% power=0.25 resistance=1k package=THT]
  R42 = Resistor [tolerance=±5% power=0.25 resistance=1k package=THT]
  R43 = Resistor [tolerance=±5% power=0.25 resistance=1k package=THT]
  R44 = Resistor [tolerance=±5% power=0.25 resistance=1k package=THT]
  R45 = Resistor [tolerance=±5% power=0.25 resistance=1k package=THT]
  R46 = Resistor [tolerance=±5% power=0.25 resistance=1k package=THT]
  R47 = Resistor [tolerance=±5% power=0.25 resistance=1k package=THT]
  R48 = Resistor [tolerance=±5% power=0.25 resistance=1k package=THT]
  D65 = 1N4148 [package=1n4148-SMD_1206]
  D66 = 1N4148 [package=1n4148-SMD_1206]
  D67 = 1N4148 [package=1n4148-SMD_1206]
  D68 = 1N4148 [package=1n4148-SMD_1206]
  D69 = 1N4148 [package=1n4148-SMD_1206]
  D70 = 1N4148 [package=1n4148-SMD_1206]
  D71 = 1N4148 [package=1n4148-SMD_1206]
  D72 = 1N4148 [package=1n4148-SMD_1206]
  D73 = 1N4148 [package=1n4148-SMD_1206]
  D74 = 1N4148 [package=1n4148-SMD_1206]
  D75 = 1N4148 [package=1n4148-SMD_1206]
  D76 = 1N4148 [package=1n4148-SMD_1206]
  D77 = 1N4148 [package=1n4148-SMD_1206]
  D78 = 1N4148 [package=1n4148-SMD_1206]
  D79 = 1N4148 [package=1n4148-SMD_1206]
  D80 = 1N4148 [package=1n4148-SMD_1206]
  D81 = 1N4148 [package=1n4148-SMD_1206]
  D82 = 1N4148 [package=1n4148-SMD_1206]
  D83 = 1N4148 [package=1n4148-SMD_1206]
  D84 = 1N4148 [package=1n4148-SMD_1206]
  D85 = 1N4148 [package=1n4148-SMD_1206]
  D86 = 1N4148 [package=1n4148-SMD_1206]
  D87 = 1N4148 [package=1n4148-SMD_1206]
  D88 = 1N4148 [package=1n4148-SMD_1206]
  D89 = 1N4148 [package=1n4148-SMD_1206]
  D90 = 1N4148 [package=1n4148-SMD_1206]
  D91 = 1N4148 [package=1n4148-SMD_1206]
  D92 = 1N4148 [package=1n4148-SMD_1206]
  D93 = 1N4148 [package=1n4148-SMD_1206]
  D94 = 1N4148 [package=1n4148-SMD_1206]
  D95 = 1N4148 [package=1n4148-SMD_1206]
  D96 = 1N4148 [package=1n4148-SMD_1206]
  R49 = Resistor [tolerance=±5% power=0.25 resistance=1k package=THT]
  R50 = Resistor [tolerance=±5% power=0.25 resistance=1k package=THT]
  R51 = Resistor [tolerance=±5% power=0.25 resistance=1k package=THT]
  R52 = Resistor [tolerance=±5% power=0.25 resistance=1k package=THT]
  R53 = Resistor [tolerance=±5% power=0.25 resistance=1k package=THT]
  R54 = Resistor [tolerance=±5% power=0.25 resistance=1k package=THT]
  R55 = Resistor [tolerance=±5% power=0.25 resistance=1k package=THT]
  R56 = Resistor [tolerance=±5% power=0.25 resistance=1k package=THT]
  R57 = Resistor [tolerance=±5% power=0.25 resistance=1k package=THT]
  R58 = Resistor [tolerance=±5% power=0.25 resistance=1k package=THT]
  R59 = Resistor [tolerance=±5% power=0.25 resistance=1k package=THT]
  R60 = Resistor [tolerance=±5% power=0.25 resistance=1k package=THT]
  R61 = Resistor [tolerance=±5% power=0.25 resistance=1k package=THT]
  R62 = Resistor [tolerance=±5% power=0.25 resistance=1k package=THT]
  R63 = Resistor [tolerance=±5% power=0.25 resistance=1k package=THT]
  R64 = Resistor [tolerance=±5% power=0.25 resistance=1k package=THT]
  R65 = Resistor [tolerance=±5% resistance=10k power=0.25 package="1206 [SMD]"]
  R66 = Resistor [tolerance=±5% resistance=10k power=0.25 package="1206 [SMD]"]
  D97 = 1N4148 [package=1n4148-SMD_1206]
  D98 = 1N4148 [package=1n4148-SMD_1206]
  D99 = 1N4148 [package=1n4148-SMD_1206]
  D100 = 1N4148 [package=1n4148-SMD_1206]
  D101 = 1N4148 [package=1n4148-SMD_1206]
  D102 = 1N4148 [package=1n4148-SMD_1206]
  D103 = 1N4148 [package=1n4148-SMD_1206]
  D104 = 1N4148 [package=1n4148-SMD_1206]
  D105 = 1N4148 [package=1n4148-SMD_1206]
  D106 = 1N4148 [package=1n4148-SMD_1206]
  D107 = 1N4148 [package=1n4148-SMD_1206]
  D108 = 1N4148 [package=1n4148-SMD_1206]
  D109 = 1N4148 [package=1n4148-SMD_1206]
  D110 = 1N4148 [package=1n4148-SMD_1206]
  D111 = 1N4148 [package=1n4148-SMD_1206]
  D112 = 1N4148 [package=1n4148-SMD_1206]
  D113 = 1N4148 [package=1n4148-SMD_1206]
  D114 = 1N4148 [package=1n4148-SMD_1206]
  D115 = 1N4148 [package=1n4148-SMD_1206]
  D116 = 1N4148 [package=1n4148-SMD_1206]
  D117 = 1N4148 [package=1n4148-SMD_1206]
  D118 = 1N4148 [package=1n4148-SMD_1206]
  D119 = 1N4148 [package=1n4148-SMD_1206]
  D120 = 1N4148 [package=1n4148-SMD_1206]
  D121 = 1N4148 [package=1n4148-SMD_1206]
  D122 = 1N4148 [package=1n4148-SMD_1206]
  D123 = 1N4148 [package=1n4148-SMD_1206]
  D124 = 1N4148 [package=1n4148-SMD_1206]
  D125 = 1N4148 [package=1n4148-SMD_1206]
  D126 = 1N4148 [package=1n4148-SMD_1206]
  D127 = 1N4148 [package=1n4148-SMD_1206]
  D128 = 1N4148 [package=1n4148-SMD_1206]
  P1 = MP1584 [part_number=MP1584-Mini package=THT]
  A2_-_I2C_Address_Select = male pin header, 3 pins [form="♂ (male)"]
  J13_-_ESP32-PoE-ISO = male pin header, 5 pins [form="♂ (male)"]
  J11_-_I2C_Expand = male pin header, 5 pins [form="♂ (male)"]

nets:
  N1: IC1.GPB0, R9.Pin_1, D17.C, D18.A
  N2: IC1.GPB1, R10.Pin_1, D19.C, D20.A
  N3: IC1.GPB2, R11.Pin_1, D21.C, D22.A
  N4: IC1.GPB3, R12.Pin_1, D23.C, D24.A
  N5: IC1.GPB04, R13.Pin_1, D25.C, D26.A
  N6: IC1.GPB5, R14.Pin_1, D27.C, D28.A
  N7: IC1.GPB6, R15.Pin_1, D29.C, D30.A
  N8: IC1.GPB8, R16.Pin_1, D31.C, D32.A
  3V3: IC1.VDD, IC1.RESET, C2.0, C1.0, IC2.VDD, IC2.A0, IC2.RESET, IC3.VDD, IC3.A1, IC3.RESET, IC4.VDD, IC4.A0, IC4.A1, IC4.RESET, C3.0, C4.0, D2.C, D4.C, D6.C, D8.C, D9.C, D11.C, D13.C, D16.C, D18.C, D20.C, D22.C, D24.C, D26.C, D28.C, D30.C, D32.C, D34.C, D36.C, D38.C, D40.C, D42.C, D44.C, D46.C, D48.C, D49.C, D52.C, D54.C, D56.C, D58.C, D59.C, D61.C, D63.C, D65.C, D68.C, D70.C, D72.C, D74.C, D76.C, D78.C, D80.C, D81.C, D84.C, D86.C, D88.C, D89.C, D91.C, D93.C, D95.C, R65.Pin_0, R66.Pin_0, D97.C, D99.C, D101.C, D103.C, D105.C, D107.C, D110.C, D112.C, D114.C, D116.C, D118.C, D120.C, D122.C, D124.C, D126.C, D128.C, A2_-_I2C_Address_Select.pin3, J13_-_ESP32-PoE-ISO.pin2, J11_-_I2C_Expand.pin2
  GND: IC1.GND, IC1.A0, IC1.A1, C2.1, C1.1, J4.pin9, J3.pin9, J2.pin9, J1.pin9, J4a.pin9, J1a.pin9, J2a.pin9, J3a.pin9, J8.pin9, J7.pin9, J5.pin9, J8a.pin9, J5a.pin9, J6.pin9, J7a.pin9, IC2.GND, IC2.A1, IC3.GND, IC3.A0, IC4.GND, C3.1, C4.1, J10.pin2, DC1.pin2, Q1.gate, D1.A, D3.A, D7.A, D10.A, D12.A, D14.A, D15.A, D17.A, D19.A, D21.A, D23.A, D5.A, D25.A, D27.A, D29.A, D31.A, J6a.pin9, D33.A, D35.A, D37.A, D39.A, D41.A, D43.A, D45.A, D47.A, D50.A, D51.A, D53.A, D55.A, D57.A, D60.A, D62.A, D64.A, D66.A, D67.A, D69.A, D71.A, D73.A, D75.A, D77.A, D79.A, D82.A, D83.A, D85.A, D87.A, D90.A, D92.A, D94.A, D96.A, D98.A, D100.A, D102.A, D104.A, D106.A, D108.A, D109.A, D111.A, D113.A, D115.A, D117.A, D119.A, D121.A, D123.A, D125.A, D127.A, P1.pin1, P1.pin2, P1.pin5, P1.pin6, A2_-_I2C_Address_Select.pin1, J13_-_ESP32-PoE-ISO.pin3, J11_-_I2C_Expand.pin3
  SCL: IC1.SCL, IC2.SCL, IC3.SCL, IC4.SCL, R65.Pin_1, J13_-_ESP32-PoE-ISO.pin4, J11_-_I2C_Expand.pin4
  SDA: IC1.SDA, IC2.SDA, IC3.SDA, IC4.SDA, R66.Pin_1, J13_-_ESP32-PoE-ISO.pin5, J11_-_I2C_Expand.pin5
  A2.: IC1.A2, IC2.A2, IC3.A2, IC4.A2, A2_-_I2C_Address_Select.pin2
  N9: IC1.GPA0, R1.Pin_1, D1.C, D2.A
  N10: IC1.GPA1, R2.Pin_1, D3.C, D4.A
  N11: IC1.GPA2, R3.Pin_1, D6.A, D5.C
  N12: IC1.GPA3, R4.Pin_1, D7.C, D8.A
  N13: IC1.GPA4, R5.Pin_1, D9.A, D10.C
  N14: IC1.GPA5, R6.Pin_1, D11.A, D12.C
  N15: IC1.GPA6, R7.Pin_1, D13.A, D14.C
  N16: IC1.GPA7, R8.Pin_1, D15.C, D16.A
  N17: J4.pin1, J4a.pin1, R32.Pin_0
  N18: J4.pin2, J4a.pin2, R31.Pin_0
  N19: J4.pin3, J4a.pin3, R30.Pin_0
  N20: J4.pin4, J4a.pin4, R29.Pin_0
  N21: J4.pin5, J4a.pin5, R28.Pin_0
  N22: J4.pin6, J4a.pin6, R27.Pin_0
  N23: J4.pin7, J4a.pin7, R26.Pin_0
  N24: J4.pin8, J4a.pin8, R25.Pin_0
  N25: J3.pin1, J3a.pin1, R24.Pin_0
  N26: J3.pin2, J3a.pin2, R23.Pin_0
  N27: J3.pin3, J3a.pin3, R22.Pin_0
  N28: J3.pin4, J3a.pin4, R21.Pin_0
  N29: J3.pin5, J3a.pin5, R20.Pin_0
  N30: J3.pin6, J3a.pin6, R19.Pin_0
  N31: J3.pin7, J3a.pin7, R18.Pin_0
  N32: J3.pin8, J3a.pin8, R17.Pin_0
  N33: J2.pin1, J2a.pin1, R16.Pin_0
  N34: J2.pin2, J2a.pin2, R15.Pin_0
  N35: J2.pin3, J2a.pin3, R14.Pin_0
  N36: J2.pin4, J2a.pin4, R13.Pin_0
  N37: J2.pin5, J2a.pin5, R12.Pin_0
  N38: J2.pin6, J2a.pin6, R11.Pin_0
  N39: J2.pin7, J2a.pin7, R10.Pin_0
  N40: J2.pin8, J2a.pin8, R9.Pin_0
  N41: J1.pin1, J1a.pin1, R8.Pin_0
  N42: J1.pin2, J1a.pin2, R7.Pin_0
  N43: J1.pin3, J1a.pin3, R6.Pin_0
  N44: J1.pin4, J1a.pin4, R5.Pin_0
  N45: J1.pin5, J1a.pin5, R4.Pin_0
  N46: J1.pin6, J1a.pin6, R3.Pin_0
  N47: J1.pin7, J1a.pin7, R2.Pin_0
  N48: J1.pin8, J1a.pin8, R1.Pin_0
  N49: J8.pin1, J8a.pin1, R64.Pin_0
  N50: J8.pin2, J8a.pin2, R63.Pin_0
  N51: J8.pin3, J8a.pin3, R62.Pin_0
  N52: J8.pin4, J8a.pin4, R61.Pin_0
  N53: J8.pin5, J8a.pin5, R60.Pin_0
  N54: J8.pin6, J8a.pin6, R59.Pin_0
  N55: J8.pin7, J8a.pin7, R58.Pin_0
  N56: J8.pin8, J8a.pin8, R57.Pin_0
  N57: J7.pin1, J7a.pin1, R56.Pin_0
  N58: J7.pin2, J7a.pin2, R55.Pin_0
  N59: J7.pin3, J7a.pin3, R54.Pin_0
  N60: J7.pin4, J7a.pin4, R53.Pin_0
  N61: J7.pin5, J7a.pin5, R52.Pin_0
  N62: J7.pin6, J7a.pin6, R51.Pin_0
  N63: J7.pin7, J7a.pin7, R50.Pin_0
  N64: J7.pin8, J7a.pin8, R49.Pin_0
  N65: J5.pin1, J5a.pin1, R40.Pin_0
  N66: J5.pin2, J5a.pin2, R39.Pin_0
  N67: J5.pin3, J5a.pin3, R38.Pin_0
  N68: J5.pin4, J5a.pin4, R37.Pin_0
  N69: J5.pin5, J5a.pin5, R36.Pin_0
  N70: J5.pin6, J5a.pin6, R35.Pin_0
  N71: J5.pin7, J5a.pin7, R34.Pin_0
  N72: J5.pin8, J5a.pin8, R33.Pin_0
  N73: J6.pin1, J6a.pin1, R48.Pin_0
  N74: J6.pin2, J6a.pin2, R47.Pin_0
  N75: J6.pin3, J6a.pin3, R46.Pin_0
  N76: J6.pin4, J6a.pin4, R45.Pin_0
  N77: J6.pin5, J6a.pin5, R44.Pin_0
  N78: J6.pin6, J6a.pin6, R43.Pin_0
  N79: J6.pin7, J6a.pin7, R42.Pin_0
  N80: J6.pin8, J6a.pin8, R41.Pin_0
  N81: IC2.GPB0, R25.Pin_1, D49.A, D50.C
  N82: IC2.GPB1, R26.Pin_1, D51.C, D52.A
  N83: IC2.GPB2, R27.Pin_1, D53.C, D54.A
  N84: IC2.GPB3, R28.Pin_1, D55.C, D56.A
  N85: IC2.GPB04, R29.Pin_1, D57.C, D58.A
  N86: IC2.GPB5, R30.Pin_1, D59.A, D60.C
  N87: IC2.GPB6, R31.Pin_1, D61.A, D62.C
  N88: IC2.GPB8, R32.Pin_1, D63.A, D64.C
  N89: IC2.GPA0, R17.Pin_1, D33.C, D34.A
  N90: IC2.GPA1, R18.Pin_1, D35.C, D36.A
  N91: IC2.GPA2, R19.Pin_1, D37.C, D38.A
  N92: IC2.GPA3, R20.Pin_1, D39.C, D40.A
  N93: IC2.GPA4, R21.Pin_1, D41.C, D42.A
  N94: IC2.GPA5, R22.Pin_1, D43.C, D44.A
  N95: IC2.GPA6, R23.Pin_1, D45.C, D46.A
  N96: IC2.GPA7, R24.Pin_1, D47.C, D48.A
  N97: IC3.GPB0, R41.Pin_1, D81.A, D82.C
  N98: IC3.GPB1, R42.Pin_1, D83.C, D84.A
  N99: IC3.GPB2, R43.Pin_1, D85.C, D86.A
  N100: IC3.GPB3, R44.Pin_1, D87.C, D88.A
  N101: IC3.GPB04, R45.Pin_1, D89.A, D90.C
  N102: IC3.GPB5, R46.Pin_1, D91.A, D92.C
  N103: IC3.GPB6, R47.Pin_1, D93.A, D94.C
  N104: IC3.GPB8, R48.Pin_1, D95.A, D96.C
  N105: IC3.GPA0, R33.Pin_1, D65.A, D66.C
  N106: IC3.GPA1, R34.Pin_1, D67.C, D68.A
  N107: IC3.GPA2, R35.Pin_1, D69.C, D70.A
  N108: IC3.GPA3, R36.Pin_1, D71.C, D72.A
  N109: IC3.GPA4, R37.Pin_1, D73.C, D74.A
  N110: IC3.GPA5, R38.Pin_1, D75.C, D76.A
  N111: IC3.GPA6, R39.Pin_1, D77.C, D78.A
  N112: IC3.GPA7, R40.Pin_1, D79.C, D80.A
  N113: IC4.GPB0, R57.Pin_1, D113.C, D114.A
  N114: IC4.GPB1, R58.Pin_1, D115.C, D116.A
  N115: IC4.GPB2, R59.Pin_1, D117.C, D118.A
  N116: IC4.GPB3, R60.Pin_1, D119.C, D120.A
  N117: IC4.GPB04, R61.Pin_1, D121.C, D122.A
  N118: IC4.GPB5, R62.Pin_1, D123.C, D124.A
  N119: IC4.GPB6, R63.Pin_1, D125.C, D126.A
  N120: IC4.GPB8, R64.Pin_1, D127.C, D128.A
  N121: IC4.GPA0, R49.Pin_1, D97.A, D98.C
  N122: IC4.GPA1, R50.Pin_1, D99.A, D100.C
  N123: IC4.GPA2, R51.Pin_1, D101.A, D102.C
  N124: IC4.GPA3, R52.Pin_1, D103.A, D104.C
  N125: IC4.GPA4, R53.Pin_1, D105.A, D106.C
  N126: IC4.GPA5, R54.Pin_1, D107.A, D108.C
  N127: IC4.GPA6, R55.Pin_1, D109.C, D110.A
  N128: IC4.GPA7, R56.Pin_1, D111.C, D112.A
  N129: J10.pin1, Q1.drain
  5V0: DC1.pin1, P1.pin7, P1.pin8, J13_-_ESP32-PoE-ISO.pin1
  VCC: DC1.pin3, Q1.source, P1.pin3, P1.pin4

notes:
  09
  14
  13
  IHC_InputBoard_010
  Rev.: 20241122 1317
  IHC Replacement Input
  SCL
  SDA
  sekt1953@gmail.com
  +5V
  GND
  +Vin
  +VCC
  00
  07
  Cat
  Ano
  01
  02
  03
  04
  05
  06
  12
  10
  11
  15
  08
  18
  23
  20
  22
  17
  19
  16
  21
  26
  31
  28
  30
  25
  27
  24
  29
  36
  37
  32
  39
  38
  33
  34
  35
  44
  45
  40
  47
  46
  41
  42
  43
  49
  52
  50
  58
  63
  59
  61
  57
  48
  54
  55
  53
  51
  60
  62
  56
  3V3
  5V
  Anode
  Catode

custom parts:
  MCP20017: MCP23017, 28 pins on a 300mil dual inline package (DIP) footprint. 16-Bit I/O Expander with I2C Serial Interface
  HW-613: DC-DC Converter, max 24V input
  1N4148: SMD 1206
  MP1584: 3A, 1.5MHz, 28V Step-Down Converter
