# Fritzing sketch Input_Board_020 (saved by Fritzing 0.9.6b)
circuit board: 10.2cm x 7.87cm
breadboards: 1

parts:
  IC2 = MCP20017 [part_number=MCP23017 package="DIP (Dual Inline) [THT]"]
  D2 = 1N4148 [package=1n4148-SMD_1206]
  D8 = 1N4148 [package=1n4148-SMD_1206]
  D7 = 1N4148 [package=1n4148-SMD_1206]
  D6 = 1N4148 [package=1n4148-SMD_1206]
  D5 = 1N4148 [package=1n4148-SMD_1206]
  D4 = 1N4148 [package=1n4148-SMD_1206]
  D3 = 1N4148 [package=1n4148-SMD_1206]
  D1 = 1N4148 [package=1n4148-SMD_1206]
  D10 = 1N4148 [package=1n4148-SMD_1206]
  D16 = 1N4148 [package=1n4148-SMD_1206]
  D15 = 1N4148 [package=1n4148-SMD_1206]
  D14 = 1N4148 [package=1n4148-SMD_1206]
  D13 = 1N4148 [package=1n4148-SMD_1206]
  D12 = 1N4148 [package=1n4148-SMD_1206]
  D11 = 1N4148 [package=1n4148-SMD_1206]
  D9 = 1N4148 [package=1n4148-SMD_1206]
  D18 = 1N4148 [package=1n4148-SMD_1206]
  D26 = 1N4148 [package=1n4148-SMD_1206]
  D24 = 1N4148 [package=1n4148-SMD_1206]
  D32 = 1N4148 [package=1n4148-SMD_1206]
  D23 = 1N4148 [package=1n4148-SMD_1206]
  D31 = 1N4148 [package=1n4148-SMD_1206]
  D22 = 1N4148 [package=1n4148-SMD_1206]
  D30 = 1N4148 [package=1n4148-SMD_1206]
  D29 = 1N4148 [package=1n4148-SMD_1206]
  D21 = 1N4148 [package=1n4148-SMD_1206]
  D28 = 1N4148 [package=1n4148-SMD_1206]
  D20 = 1N4148 [package=1n4148-SMD_1206]
  D19 = 1N4148 [package=1n4148-SMD_1206]
  D27 = 1N4148 [package=1n4148-SMD_1206]
  D25 = 1N4148 [package=1n4148-SMD_1206]
  D17 = 1N4148 [package=1n4148-SMD_1206]
  R32 = Resistor [tolerance=±5% power=0.25 resistance=220 package=THT]
  R31 = Resistor [tolerance=±5% power=0.25 resistance=220 package=THT]
  R29 = Resistor [tolerance=±5% power=0.25 resistance=220 package=THT]
  R30 = Resistor [tolerance=±5% power=0.25 resistance=220 package=THT]
  R25 = Resistor [tolerance=±5% power=0.25 resistance=220 package=THT]
  R28 = Resistor [tolerance=±5% power=0.25 resistance=220 package=THT]
  R27 = Resistor [tolerance=±5% power=0.25 resistance=220 package=THT]
  R26 = Resistor [tolerance=±5% power=0.25 resistance=220 package=THT]
  R20 = Resistor [tolerance=±5% power=0.25 resistance=220 package=THT]
  R19 = Resistor [tolerance=±5% power=0.25 resistance=220 package=THT]
  R24 = Resistor [tolerance=±5% power=0.25 resistance=220 package=THT]
  R23 = Resistor [tolerance=±5% power=0.25 resistance=220 package=THT]
  R22 = Resistor [tolerance=±5% power=0.25 resistance=220 package=THT]
  R17 = Resistor [tolerance=±5% power=0.25 resistance=220 package=THT]
  R21 = Resistor [tolerance=±5% power=0.25 resistance=220 package=THT]
  R18 = Resistor [tolerance=±5% power=0.25 resistance=220 package=THT]
  J4a = female pin header, 9 pins [form="♀ (female)"]
  J4 = female pin header, 9 pins [form="♀ (female)"]
  J3a = female pin header, 9 pins [form="♀ (female)"]
  J3 = female pin header, 9 pins [form="♀ (female)"]
  IC1 = MCP20017 [part_number=MCP23017 package="DIP (Dual Inline) [THT]"]
  D33 = 1N4148 [package=1n4148-SMD_1206]
  D34 = 1N4148 [package=1n4148-SMD_1206]
  D35 = 1N4148 [package=1n4148-SMD_1206]
  D36 = 1N4148 [package=1n4148-SMD_1206]
  D37 = 1N4148 [package=1n4148-SMD_1206]
  D38 = 1N4148 [package=1n4148-SMD_1206]
  D39 = 1N4148 [package=1n4148-SMD_1206]
  D40 = 1N4148 [package=1n4148-SMD_1206]
  D41 = 1N4148 [package=1n4148-SMD_1206]
  D42 = 1N4148 [package=1n4148-SMD_1206]
  D43 = 1N4148 [package=1n4148-SMD_1206]
  D44 = 1N4148 [package=1n4148-SMD_1206]
  D45 = 1N4148 [package=1n4148-SMD_1206]
  D46 = 1N4148 [package=1n4148-SMD_1206]
  D47 = 1N4148 [package=1n4148-SMD_1206]
  D48 = 1N4148 [package=1n4148-SMD_1206]
  D49 = 1N4148 [package=1n4148-SMD_1206]
  D50 = 1N4148 [package=1n4148-SMD_1206]
  D51 = 1N4148 [package=1n4148-SMD_1206]
  D52 = 1N4148 [package=1n4148-SMD_1206]
  D53 = 1N4148 [package=1n4148-SMD_1206]
  D54 = 1N4148 [package=1n4148-SMD_1206]
  D55 = 1N4148 [package=1n4148-SMD_1206]
  D56 = 1N4148 [package=1n4148-SMD_1206]
  D57 = 1N4148 [package=1n4148-SMD_1206]
  D58 = 1N4148 [package=1n4148-SMD_1206]
  D59 = 1N4148 [package=1n4148-SMD_1206]
  D60 = 1N4148 [package=1n4148-SMD_1206]
  D61 = 1N4148 [package=1n4148-SMD_1206]
  D62 = 1N4148 [package=1n4148-SMD_1206]
  D63 = 1N4148 [package=1n4148-SMD_1206]
  D64 = 1N4148 [package=1n4148-SMD_1206]
  R14 = Resistor [tolerance=±5% power=0.25 resistance=220 package=THT]
  R8 = Resistor [tolerance=±5% power=0.25 resistance=220 package=THT]
  R3 = Resistor [tolerance=±5% power=0.25 resistance=1k package=THT]
  R16 = Resistor [tolerance=±5% power=0.25 resistance=220 package=THT]
  R9 = Resistor [tolerance=±5% power=0.25 resistance=220 package=THT]
  R1 = Resistor [tolerance=±5% power=0.25 resistance=1k package=THT]
  R13 = Resistor [tolerance=±5% power=0.25 resistance=220 package=THT]
  R12 = Resistor [tolerance=±5% power=0.25 resistance=220 package=THT]
  R11 = Resistor [tolerance=±5% power=0.25 resistance=220 package=THT]
  R4 = Resistor [tolerance=±5% power=0.25 resistance=1k package=THT]
  R5 = Resistor [tolerance=±5% power=0.25 resistance=220 package=THT]
  R10 = Resistor [tolerance=±5% power=0.25 resistance=220 package=THT]
  R15 = Resistor [tolerance=±5% power=0.25 resistance=220 package=THT]
  R2 = Resistor [tolerance=±5% power=0.25 resistance=1k package=THT]
  R6 = Resistor [tolerance=±5% power=0.25 resistance=220 package=THT]
  R7 = Resistor [tolerance=±5% power=0.25 resistance=220 package=THT]
  J1 = female pin header, 9 pins [form="♀ (female)"]
  J2 = female pin header, 9 pins [form="♀ (female)"]
  J1a = female pin header, 9 pins [form="♀ (female)"]
  J2a = female pin header, 9 pins [form="♀ (female)"]
  C1 = Ceramic Capacitor [capacitance=100nF voltage=35V package="100 mil [THT, multilayer]"]
  C2 = Ceramic Capacitor [capacitance=100nF voltage=35V package="100 mil [THT, multilayer]"]
  J5 = female pin header, 5 pins [form="♀ (female)"]
  J6 = female pin header, 5 pins [form="♀ (female)"]
  R35 = Resistor [tolerance=±5% resistance=10k power=0.25 package="1206 [SMD]"]
  R36 = Resistor [tolerance=±5% resistance=10k power=0.25 package="1206 [SMD]"]
  R37 = Resistor [tolerance=±5% power=0.25 resistance=100k package=THT]
  R38 = Resistor [tolerance=±5% power=0.25 resistance=100k package=THT]
  A2 = female pin header, 2 pins [form="♀ (female)"]
  A1 = female pin header, 2 pins [form="♀ (female)"]
  J7 = female pin header, 31 pins [form="♀ (female)"]  # not connected
  J8 = female pin header, 2 pins [form="♀ (female)"]  # not connected
  J9 = female pin header, 14 pins [form="♀ (female)"]  # not connected
  J10 = female pin header, 2 pins [form="♀ (female)"]  # not connected
  J11 = female pin header, 2 pins [form="♀ (female)"]  # not connected

nets:
  N1: IC2.GPB0, D8.A, D24.C, R25.Pin_1
  N2: IC2.GPB1, D7.A, D23.C, R26.Pin_1
  N3: IC2.GPB2, D6.A, D22.C, R27.Pin_1
  N4: IC2.GPB3, D5.A, D21.C, R28.Pin_1
  N5: IC2.GPB04, D4.A, D20.C, R29.Pin_1
  N6: IC2.GPB5, D3.A, D19.C, R30.Pin_1
  N7: IC2.GPB6, D2.A, D18.C, R31.Pin_1
  N8: IC2.GPB8, D1.A, D17.C, R32.Pin_1
  VDD: IC2.VDD, IC2.A0, IC2.RESET, D2.C, D8.C, D7.C, D6.C, D5.C, D4.C, D3.C, D1.C, D10.C, D16.C, D15.C, D14.C, D13.C, D12.C, D11.C, D9.C, IC1.VDD, IC1.RESET, D33.C, D36.C, D37.C, D39.C, D42.C, D43.C, D45.C, D47.C, D51.C, D52.C, D53.C, D55.C, D57.C, D60.C, D61.C, D62.C, C1.0, C2.0, J5.pin3, J6.pin3, R35.Pin_1, R36.Pin_0, R37.Pin_1, R38.Pin_1
  GND: IC2.GND, IC1.GND, IC1.A0, C1.1, C2.1, J5.pin1, J6.pin1
  N9: IC2.SCL, IC1.SCL, J5.pin4, J6.pin4, R36.Pin_1
  N10: IC2.SDA, IC1.SDA, J5.pin2, J6.pin2, R35.Pin_0
  N11: IC2.A1, IC1.A1, R38.Pin_0, A1.pin2
  N12: IC2.A2, IC1.A2, R37.Pin_0, A2.pin2
  N13: IC2.GPA0, D16.A, D32.C, R17.Pin_1
  N14: IC2.GPA1, D15.A, D31.C, R18.Pin_1
  N15: IC2.GPA2, D14.A, D30.C, R19.Pin_1
  N16: IC2.GPA3, D13.A, D29.C, R20.Pin_1
  N17: IC2.GPA4, D12.A, D28.C, R21.Pin_1
  N18: IC2.GPA5, D11.A, D27.C, R22.Pin_1
  N19: IC2.GPA6, D10.A, D26.C, R23.Pin_1
  N20: IC2.GPA7, D9.A, D25.C, R24.Pin_1
  N21: D32.A, J4a.pin1, J4.pin1, J3a.pin1, J3.pin1, D34.A, D35.A, D38.A, D40.A, D41.A, D44.A, D46.A, D48.A, D49.A, D50.A, D54.A, D56.A, D58.A, D59.A, D63.A, D64.A, J1.pin1, J2.pin1, J1a.pin1, J2a.pin1, A2.pin1, A1.pin1
  N22: R32.Pin_0, J4a.pin9, J4.pin9
  N23: R31.Pin_0, J4a.pin8, J4.pin8
  N24: R29.Pin_0, J4a.pin6, J4.pin6
  N25: R30.Pin_0, J4a.pin7, J4.pin7
  N26: R25.Pin_0, J4a.pin2, J4.pin2
  N27: R28.Pin_0, J4a.pin5, J4.pin5
  N28: R27.Pin_0, J4a.pin4, J4.pin4
  N29: R26.Pin_0, J4a.pin3, J4.pin3
  N30: R20.Pin_0, J3a.pin5, J3.pin5
  N31: R19.Pin_0, J3a.pin4, J3.pin4
  N32: R24.Pin_0, J3a.pin9, J3.pin9
  N33: R23.Pin_0, J3a.pin8, J3.pin8
  N34: R22.Pin_0, J3a.pin7, J3.pin7
  N35: R17.Pin_0, J3a.pin2, J3.pin2
  N36: R21.Pin_0, J3a.pin6, J3.pin6
  N37: R18.Pin_0, J3a.pin3, J3.pin3
  N38: IC1.GPB0, D38.C, D39.A, R9.Pin_1
  N39: IC1.GPB1, D43.A, D44.C, R10.Pin_1
  N40: IC1.GPB2, D45.A, D46.C, R11.Pin_1
  N41: IC1.GPB3, D50.C, D51.A, R12.Pin_1
  N42: IC1.GPB04, D53.A, D54.C, R13.Pin_1
  N43: IC1.GPB5, D59.C, D60.A, R14.Pin_1
  N44: IC1.GPB6, D34.C, D36.A, R15.Pin_1
  N45: IC1.GPB8, D62.A, D63.C, R16.Pin_1
  N46: IC1.GPA0, D37.A, D40.C, R1.Pin_1
  N47: IC1.GPA1, D41.C, D42.A, R2.Pin_1
  N48: IC1.GPA2, D47.A, D48.C, R3.Pin_1
  N49: IC1.GPA3, D49.C, D52.A, R4.Pin_1
  N50: IC1.GPA4, D55.A, D56.C, R5.Pin_1
  N51: IC1.GPA5, D57.A, D58.C, R6.Pin_1
  N52: IC1.GPA6, D33.A, D35.C, R7.Pin_1
  N53: IC1.GPA7, D61.A, D64.C, R8.Pin_1
  N54: R14.Pin_0, J2.pin7, J2a.pin7
  N55: R8.Pin_0, J1.pin9, J1a.pin9
  N56: R3.Pin_0, J1.pin4, J1a.pin4
  N57: R16.Pin_0, J2.pin9, J2a.pin9
  N58: R9.Pin_0, J2.pin2, J2a.pin2
  N59: R1.Pin_0, J1.pin2, J1a.pin2
  N60: R13.Pin_0, J2.pin6, J2a.pin6
  N61: R12.Pin_0, J2.pin5, J2a.pin5
  N62: R11.Pin_0, J2.pin4, J2a.pin4
  N63: R4.Pin_0, J1.pin5, J1a.pin5
  N64: R5.Pin_0, J1.pin6, J1a.pin6
  N65: R10.Pin_0, J2.pin3, J2a.pin3
  N66: R15.Pin_0, J2.pin8, J2a.pin8
  N67: R2.Pin_0, J1.pin3, J1a.pin3
  N68: R6.Pin_0, J1.pin7, J1a.pin7
  N69: R7.Pin_0, J1.pin8, J1a.pin8
  N70: J5.pin5, J6.pin5

notes:
  Gnd
  Sda
  +3V3
  Scl
  +12v
  A
  Cat

custom parts:
  MCP20017: MCP23017, 28 pins on a 300mil dual inline package (DIP) footprint. 16-Bit I/O Expander with I2C Serial Interface
  1N4148: SMD 1206
