# Fritzing sketch Output_Board_010 (saved by Fritzing 0.9.6b)
circuit board: 20.95cm x 8cm
breadboards: 1

parts:
  IC1 = MCP20017 [part_number=MCP23017 package="DIP (Dual Inline) [THT]"]
  C2 = Ceramic Capacitor [capacitance=100nF voltage=35V package="100 mil [THT, multilayer]"]
  C1 = Ceramic Capacitor [capacitance=100nF voltage=35V package="100 mil [THT, multilayer]"]
  J4 = female pin header, 9 pins [form="♀ (female)"]
  J3 = female pin header, 9 pins [form="♀ (female)"]
  J2 = female pin header, 9 pins [form="♀ (female)"]
  J1 = female pin header, 9 pins [form="♀ (female)"]
  J4a = female pin header, 9 pins [form="♀ (female)"]
  J1a = female pin header, 9 pins [form="♀ (female)"]
  J2a = female pin header, 9 pins [form="♀ (female)"]
  J3a = female pin header, 9 pins [form="♀ (female)"]
  J8 = female pin header, 9 pins [form="♀ (female)"]
  J7 = female pin header, 9 pins [form="♀ (female)"]
  J5 = female pin header, 9 pins [form="♀ (female)"]
  J8a = female pin header, 9 pins [form="♀ (female)"]
  J5a = female pin header, 9 pins [form="♀ (female)"]
  J6 = female pin header, 9 pins [form="♀ (female)"]
  J7a = female pin header, 9 pins [form="♀ (female)"]
  IC2 = MCP20017 [part_number=MCP23017 package="DIP (Dual Inline) [THT]"]
  IC3 = MCP20017 [part_number=MCP23017 package="DIP (Dual Inline) [THT]"]
  IC4 = MCP20017 [part_number=MCP23017 package="DIP (Dual Inline) [THT]"]
  C3 = Ceramic Capacitor [capacitance=100nF voltage=35V package="100 mil [THT, multilayer]"]
  C4 = Ceramic Capacitor [capacitance=100nF voltage=35V package="100 mil [THT, multilayer]"]
  J10 = Screw terminal - 2 pins [package=THT]
  DC1 = HW-613 [part_number=HW-613-5V package=THT]
  Q1 = Basic FET P-Channel [part_number=FQP27P06 package="TO220 [THT]"]
  J6a = female pin header, 9 pins [form="♀ (female)"]
  R65 = Resistor [tolerance=±5% resistance=10k power=0.25 package="1206 [SMD]"]
  R66 = Resistor [tolerance=±5% resistance=10k power=0.25 package="1206 [SMD]"]
  P1 = MP1584 [part_number=MP1584-Mini package=THT]
  IO2 = ULN2803A [form="♂ (male)" part_number=ULN2803a package=THT]
  IO1 = ULN2803A [form="♂ (male)" part_number=ULN2803a package=THT]
  IO4 = ULN2803A [form="♂ (male)" part_number=ULN2803a package=THT]
  IO3 = ULN2803A [form="♂ (male)" part_number=ULN2803a package=THT]
  IO5 = ULN2803A [form="♂ (male)" part_number=ULN2803a package=THT]
  IO6 = ULN2803A [form="♂ (male)" part_number=ULN2803a package=THT]
  IO7 = ULN2803A [form="♂ (male)" part_number=ULN2803a package=THT]
  IO8 = ULN2803A [form="♂ (male)" part_number=ULN2803a package=THT]
  A2_-_I2C_Address_Select = male pin header, 3 pins [form="♂ (male)"]
  J13_-ESP32_PoE-_ISO = male pin header, 5 pins [form="♂ (male)"]
  J11_-_I2C_Expand = male pin header, 5 pins [form="♂ (male)"]

nets:
  N1: IC1.GPB0, IO2.pin8
  N2: IC1.GPB1, IO2.pin7
  N3: IC1.GPB2, IO2.pin6
  N4: IC1.GPB3, IO2.pin5
  N5: IC1.GPB04, IO2.pin4
  N6: IC1.GPB5, IO2.pin3
  N7: IC1.GPB6, IO2.pin2
  N8: IC1.GPB8, IO2.pin1
  3V3: IC1.VDD, IC1.RESET, C2.0, C1.0, IC2.VDD, IC2.A0, IC2.RESET, IC3.VDD, IC3.A1, IC3.RESET, IC4.VDD, IC4.A0, IC4.A1, IC4.RESET, C3.0, C4.0, R65.Pin_0, R66.Pin_0, A2_-_I2C_Address_Select.pin3, J13_-ESP32_PoE-_ISO.pin2, J11_-_I2C_Expand.pin2
  GND: IC1.GND, IC1.A0, IC1.A1, C2.1, C1.1, IC2.GND, IC2.A1, IC3.GND, IC3.A0, IC4.GND, C3.1, C4.1, J10.pin2, DC1.pin2, Q1.gate, P1.pin1, P1.pin2, P1.pin5, P1.pin6, IO2.pin9, IO1.pin9, IO4.pin9, IO3.pin9, IO5.pin9, IO6.pin9, IO7.pin9, IO8.pin9, A2_-_I2C_Address_Select.pin1, J13_-ESP32_PoE-_ISO.pin3, J11_-_I2C_Expand.pin3
  SCL: IC1.SCL, IC2.SCL, IC3.SCL, IC4.SCL, R65.Pin_1, J13_-ESP32_PoE-_ISO.pin4, J11_-_I2C_Expand.pin4
  SDA: IC1.SDA, IC2.SDA, IC3.SDA, IC4.SDA, R66.Pin_1, J13_-ESP32_PoE-_ISO.pin5, J11_-_I2C_Expand.pin5
  A2.: IC1.A2, IC2.A2, IC3.A2, IC4.A2, A2_-_I2C_Address_Select.pin2
  N9: IC1.GPA0, IO1.pin8
  N10: IC1.GPA1, IO1.pin7
  N11: IC1.GPA2, IO1.pin6
  N12: IC1.GPA3, IO1.pin5
  N13: IC1.GPA4, IO1.pin4
  N14: IC1.GPA5, IO1.pin3
  N15: IC1.GPA6, IO1.pin2
  N16: IC1.GPA7, IO1.pin1
  N17: J4.pin1, J4a.pin1, IO4.pin18
  N18: J4.pin2, J4a.pin2, IO4.pin17
  N19: J4.pin3, J4a.pin3, IO4.pin16
  N20: J4.pin4, J4a.pin4, IO4.pin15
  N21: J4.pin5, J4a.pin5, IO4.pin14
  N22: J4.pin6, J4a.pin6, IO4.pin13
  N23: J4.pin7, J4a.pin7, IO4.pin12
  N24: J4.pin8, J4a.pin8, IO4.pin11
  VCC: J4.pin9, J3.pin9, J2.pin9, J1.pin9, J4a.pin9, J1a.pin9, J2a.pin9, J3a.pin9, J8.pin9, J7.pin9, J5.pin9, J8a.pin9, J5a.pin9, J6.pin9, J7a.pin9, DC1.pin3, Q1.source, J6a.pin9, P1.pin3, P1.pin4, IO2.pin10, IO1.pin10, IO4.pin10, IO3.pin10, IO5.pin10, IO6.pin10, IO7.pin10, IO8.pin10
  N25: J3.pin1, J3a.pin1, IO3.pin18
  N26: J3.pin2, J3a.pin2, IO3.pin17
  N27: J3.pin3, J3a.pin3, IO3.pin16
  N28: J3.pin4, J3a.pin4, IO3.pin15
  N29: J3.pin5, J3a.pin5, IO3.pin14
  N30: J3.pin6, J3a.pin6, IO3.pin13
  N31: J3.pin7, J3a.pin7, IO3.pin12
  N32: J3.pin8, J3a.pin8, IO3.pin11
  N33: J2.pin1, J2a.pin1, IO2.pin18
  N34: J2.pin2, J2a.pin2, IO2.pin17
  N35: J2.pin3, J2a.pin3, IO2.pin16
  N36: J2.pin4, J2a.pin4, IO2.pin15
  N37: J2.pin5, J2a.pin5, IO2.pin14
  N38: J2.pin6, J2a.pin6, IO2.pin13
  N39: J2.pin7, J2a.pin7, IO2.pin12
  N40: J2.pin8, J2a.pin8, IO2.pin11
  N41: J1.pin1, J1a.pin1, IO1.pin18
  N42: J1.pin2, J1a.pin2, IO1.pin17
  N43: J1.pin3, J1a.pin3, IO1.pin16
  N44: J1.pin4, J1a.pin4, IO1.pin15
  N45: J1.pin5, J1a.pin5, IO1.pin14
  N46: J1.pin6, J1a.pin6, IO1.pin13
  N47: J1.pin7, J1a.pin7, IO1.pin12
  N48: J1.pin8, J1a.pin8, IO1.pin11
  N49: J8.pin1, J8a.pin1, IO8.pin18
  N50: J8.pin2, J8a.pin2, IO8.pin17
  N51: J8.pin3, J8a.pin3, IO8.pin16
  N52: J8.pin4, J8a.pin4, IO8.pin15
  N53: J8.pin5, J8a.pin5, IO8.pin14
  N54: J8.pin6, J8a.pin6, IO8.pin13
  N55: J8.pin7, J8a.pin7, IO8.pin12
  N56: J8.pin8, J8a.pin8, IO8.pin11
  N57: J7.pin1, J7a.pin1, IO7.pin18
  N58: J7.pin2, J7a.pin2, IO7.pin17
  N59: J7.pin3, J7a.pin3, IO7.pin16
  N60: J7.pin4, J7a.pin4, IO7.pin15
  N61: J7.pin5, J7a.pin5, IO7.pin14
  N62: J7.pin6, J7a.pin6, IO7.pin13
  N63: J7.pin7, J7a.pin7, IO7.pin12
  N64: J7.pin8, J7a.pin8, IO7.pin11
  N65: J5.pin1, J5a.pin1, IO5.pin18
  N66: J5.pin2, J5a.pin2, IO5.pin17
  N67: J5.pin3, J5a.pin3, IO5.pin16
  N68: J5.pin4, J5a.pin4, IO5.pin15
  N69: J5.pin5, J5a.pin5, IO5.pin14
  N70: J5.pin6, J5a.pin6, IO5.pin13
  N71: J5.pin7, J5a.pin7, IO5.pin12
  N72: J5.pin8, J5a.pin8, IO5.pin11
  N73: J6.pin1, J6a.pin1, IO6.pin18
  N74: J6.pin2, J6a.pin2, IO6.pin17
  N75: J6.pin3, J6a.pin3, IO6.pin16
  N76: J6.pin4, J6a.pin4, IO6.pin15
  N77: J6.pin5, J6a.pin5, IO6.pin14
  N78: J6.pin6, J6a.pin6, IO6.pin13
  N79: J6.pin7, J6a.pin7, IO6.pin12
  N80: J6.pin8, J6a.pin8, IO6.pin11
  N81: IC2.GPB0, IO4.pin8
  N82: IC2.GPB1, IO4.pin7
  N83: IC2.GPB2, IO4.pin6
  N84: IC2.GPB3, IO4.pin5
  N85: IC2.GPB04, IO4.pin4
  N86: IC2.GPB5, IO4.pin3
  N87: IC2.GPB6, IO4.pin2
  N88: IC2.GPB8, IO4.pin1
  N89: IC2.GPA0, IO3.pin8
  N90: IC2.GPA1, IO3.pin7
  N91: IC2.GPA2, IO3.pin6
  N92: IC2.GPA3, IO3.pin5
  N93: IC2.GPA4, IO3.pin4
  N94: IC2.GPA5, IO3.pin3
  N95: IC2.GPA6, IO3.pin2
  N96: IC2.GPA7, IO3.pin1
  N97: IC3.GPB0, IO6.pin8
  N98: IC3.GPB1, IO6.pin7
  N99: IC3.GPB2, IO6.pin6
  N100: IC3.GPB3, IO6.pin5
  N101: IC3.GPB04, IO6.pin4
  N102: IC3.GPB5, IO6.pin3
  N103: IC3.GPB6, IO6.pin2
  N104: IC3.GPB8, IO6.pin1
  N105: IC3.GPA0, IO5.pin8
  N106: IC3.GPA1, IO5.pin7
  N107: IC3.GPA2, IO5.pin6
  N108: IC3.GPA3, IO5.pin5
  N109: IC3.GPA4, IO5.pin4
  N110: IC3.GPA5, IO5.pin3
  N111: IC3.GPA6, IO5.pin2
  N112: IC3.GPA7, IO5.pin1
  N113: IC4.GPB0, IO8.pin8
  N114: IC4.GPB1, IO8.pin7
  N115: IC4.GPB2, IO8.pin6
  N116: IC4.GPB3, IO8.pin5
  N117: IC4.GPB04, IO8.pin4
  N118: IC4.GPB5, IO8.pin3
  N119: IC4.GPB6, IO8.pin2
  N120: IC4.GPB8, IO8.pin1
  N121: IC4.GPA0, IO7.pin8
  N122: IC4.GPA1, IO7.pin7
  N123: IC4.GPA2, IO7.pin6
  N124: IC4.GPA3, IO7.pin5
  N125: IC4.GPA4, IO7.pin4
  N126: IC4.GPA5, IO7.pin3
  N127: IC4.GPA6, IO7.pin2
  N128: IC4.GPA7, IO7.pin1
  N129: J10.pin1, Q1.drain
  5V0: DC1.pin1, P1.pin7, P1.pin8, J13_-ESP32_PoE-_ISO.pin1

notes:
  09
  14
  13
  IHC_OutputBoard_010
  Rev.: 20241118 1210
  IHC Replacement Output
  SCL
  SDA
  sekt1953@gmail.com
  +5V
  GND
  +Vin
  +VCC
  00
  07
  Vcc
  01
  02
  03
  04
  05
  06
  12
  10
  11
  15
  08
  18
  23
  20
  22
  17
  19
  16
  21
  26
  31
  28
  30
  25
  27
  24
  29
  36
  37
  32
  39
  38
  33
  34
  35
  44
  45
  40
  47
  46
  41
  42
  43
  49
  52
  50
  58
  63
  59
  61
  57
  48
  54
  55
  53
  51
  60
  62
  56
  3V3
  5V

custom parts:
  MCP20017: MCP23017, 28 pins on a 300mil dual inline package (DIP) footprint. 16-Bit I/O Expander with I2C Serial Interface
  HW-613: DC-DC Converter, max 24V input
  MP1584: 3A, 1.5MHz, 28V Step-Down Converter
  ULN2803A: Generic male header
